// Logisim project alu32.circ as structural Verilog: 1 circuit, main circuit main
module main (
  input  [31:0] A,
  input  [31:0] B,
  input  [2:0] F,
  output [31:0] Y
);

  wire [30:0] adder_1_out;
  wire [31:0] and_1_out, bit_extender_1_out, multiplexer_1_out, not_1_out, or_1_out;
  wire [31:31] adder_1_out_2;

  assign not_1_out = ~B;  // NOT_Gate not_1, 32 bits wide
  Multiplexer #(.width(32)) multiplexer_1 (.in0(B), .in1(not_1_out), .out(multiplexer_1_out), .sel(F[2]));  // open: en
  assign and_1_out = A & multiplexer_1_out;  // AND_Gate and_1, 32 bits wide
  assign or_1_out = A | multiplexer_1_out;  // OR_Gate or_1, 32 bits wide
  Adder #(.width(32)) adder_1 (
    .a(A), .b(multiplexer_1_out), .out({adder_1_out_2[31], adder_1_out}), .cin(F[2]));  // open: cout
  assign bit_extender_1_out = {{31{1'b0}}, adder_1_out_2[31]};  // Bit_Extender bit_extender_1
  Multiplexer #(.select(2), .width(32)) multiplexer_2 (
    .in0(and_1_out), .in1(or_1_out), .in2({adder_1_out_2[31], adder_1_out}), .in3(bit_extender_1_out),
    .out(Y), .sel(F[1:0]));  // open: en

  // Notes on the sheet:
  //   1 if A - B < 0
endmodule
