// Logisim project datamem.circ as structural Verilog: 1 circuit, main circuit main
module main (
  input  [8:0] A,
  input  CLK,
  input  MemWrite,
  input  [31:0] WD,
  output [31:0] RD
);

  wire not_1_out;

  not not_1 (not_1_out, MemWrite);
  RAM #(.addrWidth(7), .dataWidth(32)) ram_1 (.addr(A[8:2]), .data(RD), .clk(CLK), .ld(not_1_out));  // open: sel, clr
  assign RD = MemWrite ? WD : 32'bz;  // Controlled_Buffer controlled_buffer_1

  // Notes on the sheet:
  //   ld: 1 --> Memory Value --> RD
endmodule
