// Logisim project mips_lw.circ as structural Verilog: 1 circuit, main circuit main
module main (
  input  in_1
);

  wire clock_1_out;
  wire [1:0] register_1_q;
  wire [5:0] register_1_q_2;
  wire [7:0] adder_1_out;
  wire [31:0] adder_2_out, bit_extender_1_out, main_1_rd1, ram_1_data, rom_1_data;

  Clock clock_1 (.out(clock_1_out));
  Register register_1 (.D(adder_1_out), .Q({register_1_q_2, register_1_q}), .clk(clock_1_out));  // open: en, clr
  Adder adder_1 (.a({register_1_q_2, register_1_q}), .b(8'h4), .out(adder_1_out));  // open: cin, cout
  ROM #(.addrWidth(6), .dataWidth(32)) rom_1 (.addr(register_1_q_2), .data(rom_1_data));  // open: sel
  // Probe on rom_1_data[20:16]
  // Probe on rom_1_data[31:26]
  RegFile_main main_1 (
    .A1(rom_1_data[25:21]), .in_3(clock_1_out), .A3(rom_1_data[20:16]), .WD3(ram_1_data), .in_6(in_1),
    .RD1(main_1_rd1));  // open: A2, RD2
  assign bit_extender_1_out = {{16{rom_1_data[15]}}, rom_1_data[15:0]};  // Bit_Extender bit_extender_1
  Adder #(.width(32)) adder_2 (.a(main_1_rd1), .b(bit_extender_1_out), .out(adder_2_out));  // open: cin, cout
  RAM #(.addrWidth(7), .dataWidth(32)) ram_1 (.addr(adder_2_out[8:2]), .data(ram_1_data));  // open: sel, clk, ld, clr

  // Notes on the sheet:
  //   lw  $t2,  32($0)
  //   contents of rom_1 (hex, n*v repeats v):
  //   8c0a0020 8c0a0020 14b4820
endmodule
